# Fritzing sketch gpio-2 (saved by Fritzing 0.9.2b)
breadboards: 1

parts:
  Raspberry_Pi1 = Raspberry Pi 2
  R1 = Resistor [tolerance=±5% resistance=220 package=THT]
  S1 = Pushbutton [package="[SMD]"]
  LED1 = LED - 5mm [color="Red (633nm)" package="5 mm [THT]"]

nets:
  3V3: Raspberry_Pi1.3v3, Raspberry_Pi1.3V3, Raspberry_Pi1.GPIO23, R1.Pin_1, S1.Pin_1, S1.Pin_2, S1.Pin_3, S1.Pin_4
  N1: Raspberry_Pi1.GND, R1.Pin_0, LED1.cathode, LED1.anode
