# Fritzing sketch gpio-mcp23008-interrupt test (saved by Fritzing 0.9.2b)
breadboards: 1

parts:
  IC1 = Microchip MCP23008 8-bit I/O expander [part_number=MCP23008 package="DIP (Dual Inline) [THT]"]
  Raspberry_Pi1 = Raspberry Pi 2
  R1 = Resistor [tolerance=±5% resistance=220 package=THT]
  R2 = Resistor [tolerance=±5% resistance=220 package=THT]
  R7 = Resistor [tolerance=±5% resistance=220 package=THT]
  R9 = Resistor [tolerance=±5% resistance=220 package=THT]
  LED1 = LED - 5mm [color="Red (633nm)" package="5 mm [THT]"]
  LED2 = LED - 5mm [color="Red (633nm)" package="5 mm [THT]"]
  LED3 = LED - 5mm [color="Red (633nm)" package="5 mm [THT]"]
  LED4 = LED - 5mm [color="Red (633nm)" package="5 mm [THT]"]

nets:
  N1: IC1.SCL, Raspberry_Pi1.GPIO3
  N2: IC1.SDA, Raspberry_Pi1.GPIO2
  VSS: IC1.A2, IC1.A1, IC1.A0, IC1.VSS, Raspberry_Pi1.GND, LED1.cathode, LED2.cathode, LED3.cathode, LED4.cathode
  VDD: IC1.Reset, IC1.VDD, Raspberry_Pi1.5V
  N3: IC1.INT, Raspberry_Pi1.GPIO27
  N4: IC1.GP0, IC1.GP4, R9.Pin_1
  N5: IC1.GP1, IC1.GP5, R7.Pin_1
  N6: IC1.GP2, IC1.GP6, R2.Pin_1
  N7: IC1.GP3, IC1.GP7, R1.Pin_1
  N8: R1.Pin_0, LED4.anode
  N9: R2.Pin_0, LED3.anode
  N10: R7.Pin_0, LED2.anode
  N11: R9.Pin_0, LED1.anode

custom parts:
  Microchip MCP23008 8-bit I/O expander: Provides 8-bit, general purpose, parallel I/O expansion for I2C bus. Datasheet: http://ww1.microchip.com/downloads/en/devicedoc/21919e.pdf
