# Fritzing sketch gpio-multi mcp23008 (saved by Fritzing 0.9.2b)
breadboards: 1

parts:
  IC1 = Microchip MCP23008 8-bit I/O expander [part_number=MCP23008 package="DIP (Dual Inline) [THT]"]
  IC2 = Microchip MCP23008 8-bit I/O expander [part_number=MCP23008 package="DIP (Dual Inline) [THT]"]
  Raspberry_Pi1 = Raspberry Pi 2

nets:
  N1: IC1.SCL, IC2.SCL, Raspberry_Pi1.GPIO3
  N2: IC1.SDA, IC2.SDA, Raspberry_Pi1.GPIO2
  VSS: IC1.A2, IC1.A1, IC1.VSS, IC2.A2, IC2.A1, IC2.A0, IC2.VSS, Raspberry_Pi1.GND
  VDD: IC1.A0, IC1.Reset, IC1.VDD, IC2.Reset, IC2.VDD, Raspberry_Pi1.5V

custom parts:
  Microchip MCP23008 8-bit I/O expander: Provides 8-bit, general purpose, parallel I/O expansion for I2C bus. Datasheet: http://ww1.microchip.com/downloads/en/devicedoc/21919e.pdf
