# Fritzing sketch gpio-pwm (saved by Fritzing 0.9.2b)
breadboards: 1

parts:
  Raspberry_Pi1 = Raspberry Pi 2
  R1 = Resistor [tolerance=±5% resistance=220 package=THT]
  LED1 = LED - 5mm [color="Red (633nm)" package="5 mm [THT]"]
  R2 = Resistor [tolerance=±5% resistance=220 package=THT]
  LED2 = LED - 5mm [color="Red (633nm)" package="5 mm [THT]"]

nets:
  N1: Raspberry_Pi1.GPIO13, R2.Pin_1
  N2: Raspberry_Pi1.GND, R1.Pin_0, LED1.cathode, LED1.anode, R2.Pin_0, LED2.cathode, LED2.anode
  N3: Raspberry_Pi1.GPIO18, R1.Pin_1
