# Fritzing sketch led (saved by Fritzing 0.9.3b)
breadboards: 1

parts:
  S1 = Round Pushbutton
  LED1 = LED - 3mm [color="Red (633nm)" package="3 mm [THT]"]
  R1 = Resistor [tolerance=±5% resistance=220 package="0402 [SMD]"]
  Raspberry_Pi_1 = Raspberry Pi 3 [part_number=RPI-3-V1.2]

nets (from the breadboard view):
  N1: S1.leg0, LED1.anode
  N2: S1.leg1, Raspberry_Pi_1.3v3
  N3: LED1.cathode, R1.Pin_1
  N4: R1.Pin_0, Raspberry_Pi_1.GND
