# Fritzing sketch BMP180 (saved by Fritzing 0.9.2b)

parts:
  BMP1 = BMP180
  Raspberry_Pi1 = Raspberry Pi 2

nets:
  VIN: BMP1.VIN, Raspberry_Pi1.3v3
  N1: BMP1.SCL, Raspberry_Pi1.GPIO3
  N2: BMP1.SDA, Raspberry_Pi1.GPIO2
  GND: BMP1.GND, Raspberry_Pi1.GND
