# Fritzing sketch Pi (saved by Fritzing 0.9.2b)

parts:
  Raspberry_Pi1 = Raspberry Pi 2
  PIR1 = PIR sensor
  M1 = Stepper Motor - Unipolar
  VCC1 = 4 x AAA Battery Mount

nets:
  N1: Raspberry_Pi1.GPIO4, M1.COMMON_1
  N2: Raspberry_Pi1.GPIO17, M1.C
  N3: Raspberry_Pi1.GPIO27, M1.B
  N4: Raspberry_Pi1.GPIO22, M1.COMMON_2
  N5: Raspberry_Pi1.GPIO23, PIR1.SIG
  GND: Raspberry_Pi1.GND, PIR1.GND
  5V: Raspberry_Pi1.5V, PIR1.VDD
  N6: M1.A, VCC1.+
  N7: M1.D, VCC1.-
