# Fritzing sketch arduino (saved by Fritzing 0.9.2b)

parts:
  부품1 = Arduino Nano (Rev3.0)
  U1 = GAS_SENSOR [package=mq-3]
  부품2 = Bluetooth HC-05 Macho
  VCC1 = 4 x AAA Battery Mount
  DHT1 = DHT11 Humitidy and Temperature Sensor

nets:
  GND: 부품1.GND, U1.A1, 부품2.GND, VCC1.-, DHT1.GND
  N1: 부품1.D4, DHT1.DATA
  N2: 부품1.D10, 부품2.TXD
  N3: 부품1.D11/MOSI, 부품2.RXD
  N4: 부품1.VIN, VCC1.+
  5V: 부품1.5V, U1.B1, 부품2.VCC, DHT1.VDD

custom parts:
  DHT11 Humitidy and Temperature Sensor: DHT11 Humidity and Temperature Sensor
