# Fritzing sketch audio input - comment (saved by Fritzing 0.9.2b)
circuit board: 4.72722cm x 5.43278cm
breadboards: 1

parts:
  R9 = Resistor [tolerance=±5% resistance=100k package=THT]
  TRS2 = Audio Jack (TRS) 3.5mm [package="4Ucon 08780 [THT]"]
  Raspberry_Pi1 = Raspberry Pi 2
  R11 = Resistor [tolerance=±5% resistance=22k package=THT]
  R12 = Resistor [tolerance=±5% resistance=22k package=THT]
  MSGEQ3 = MSGEQ7 Chip [package=THT]
  C5 = Ceramic Capacitor [capacitance=10nF package="100 mil [THT, multilayer]"]
  C6 = Ceramic Capacitor [capacitance=10nF package="100 mil [THT, multilayer]"]
  C7 = Ceramic Capacitor [capacitance=100nF package="100 mil [THT, multilayer]"]
  C8 = Ceramic Capacitor [capacitance=100nF package="100 mil [THT, multilayer]"]
  R13 = Resistor [tolerance=±5% resistance=100k package=THT]
  C9 = Ceramic Capacitor [capacitance=100nF package="100 mil [THT, multilayer]"]
  MSGEQ4 = MSGEQ7 Chip [package=THT]
  C10 = Ceramic Capacitor [capacitance=100nF package="100 mil [THT, multilayer]"]
  R14 = Resistor [tolerance=±5% resistance=100k package=THT]
  R15 = Resistor [tolerance=±5% resistance=100k package=THT]
  C11 = Ceramic Capacitor [capacitance=100nF package="100 mil [THT, multilayer]"]
  C12 = Ceramic Capacitor [capacitance=100nF package="100 mil [THT, multilayer]"]
  IC2 = MCP3008 8-channel 10-bit ADC [part_number=MCP3008]

nets:
  N1: R9.Pin_0, R13.Pin_0
  VDD: R9.Pin_1, Raspberry_Pi1.5V, MSGEQ3.VDD, C7.1, MSGEQ4.VDD, C10.1, R14.Pin_1, IC2.no_name_yet#15, IC2.no_name_yet#16
  GND: TRS2.Sleeve, Raspberry_Pi1.GND, C7.0, C8.0, C9.0, MSGEQ4.VSS, C10.0, C11.0, C12.0, IC2.no_name_yet#9, IC2.no_name_yet#14
  N2: TRS2.Ring, TRS2.Tip, R11.Pin_1, R12.Pin_1
  N3: Raspberry_Pi1.GPIO17, MSGEQ3.RESET, MSGEQ4.RESET
  N4: Raspberry_Pi1.GPIO27, MSGEQ3.STROBE, MSGEQ4.STROBE
  N5: Raspberry_Pi1.GPIO10, IC2.no_name_yet#11
  N6: Raspberry_Pi1.GPIO9, IC2.no_name_yet#12
  N7: Raspberry_Pi1.GPIO11, IC2.no_name_yet#13
  N8: Raspberry_Pi1.GPIO8, IC2.no_name_yet#10
  N9: R11.Pin_0, C5.1
  N10: R12.Pin_0, C6.1
  N11: MSGEQ3.OUT, IC2.no_name_yet#2
  N12: MSGEQ3.IN, C5.0
  N13: MSGEQ3.GND, C8.1
  N14: MSGEQ3.CKIN, R13.Pin_1, C9.1
  N15: C6.0, MSGEQ4.IN
  N16: MSGEQ4.OUT, IC2.no_name_yet#1
  N17: MSGEQ4.GND, C12.1
  N18: MSGEQ4.CKIN, R15.Pin_1, C11.1
  N19: R14.Pin_0, R15.Pin_0

notes:
  3.5mm   Audio INPUT
  Left Channel
  Right Channel
  0.01uF
  33pF
  0.1uF
  AD 변환
  RESET을 GPIO17에 연결
  STROBE를 GPIO27에 연결
  SPI 통신
  100kΩ 2개
  100Ω 2개
  22kΩ
  접지

custom parts:
  MSGEQ7 Chip: Seven Band Graphic Equalizer
