# Fritzing sketch led matrix (saved by Fritzing 0.9.2b)

parts:
  U2 = 74HC595 [package="DIP16 [THT]"]
  U3 = 74HC595 [package="DIP16 [THT]"]
  VCC1 = 4 x AAA Battery Mount  # not connected
  U4 = 74HC595 [package="DIP16 [THT]"]
  U5 = 74HC595 [package="DIP16 [THT]"]
  R9 = Resistor [tolerance=±5% resistance=330 package=THT]
  R10 = Resistor [tolerance=±5% resistance=330 package=THT]
  R11 = Resistor [tolerance=±5% resistance=330 package=THT]
  R12 = Resistor [tolerance=±5% resistance=330 package=THT]
  R13 = Resistor [tolerance=±5% resistance=330 package=THT]
  R14 = Resistor [tolerance=±5% resistance=330 package=THT]
  R15 = Resistor [tolerance=±5% resistance=330 package=THT]
  R16 = Resistor [tolerance=±5% resistance=330 package=THT]
  R17 = Resistor [tolerance=±5% resistance=330 package=THT]
  R18 = Resistor [tolerance=±5% resistance=330 package=THT]
  R19 = Resistor [tolerance=±5% resistance=330 package=THT]
  R20 = Resistor [tolerance=±5% resistance=330 package=THT]
  R21 = Resistor [tolerance=±5% resistance=330 package=THT]
  R22 = Resistor [tolerance=±5% resistance=330 package=THT]
  R23 = Resistor [tolerance=±5% resistance=330 package=THT]
  R24 = Resistor [tolerance=±5% resistance=330 package=THT]
  R25 = Resistor [tolerance=±5% resistance=330 package=THT]
  R26 = Resistor [tolerance=±5% resistance=330 package=THT]
  R27 = Resistor [tolerance=±5% resistance=330 package=THT]
  R28 = Resistor [tolerance=±5% resistance=330 package=THT]
  R29 = Resistor [tolerance=±5% resistance=330 package=THT]
  R30 = Resistor [tolerance=±5% resistance=330 package=THT]
  R31 = Resistor [tolerance=±5% resistance=330 package=THT]
  R32 = Resistor [tolerance=±5% resistance=330 package=THT]
  UDN_2981_-_8-Channel_Source_Driver2 = DIP - 18 pins [package="DIP (Dual Inline) [THT]"]

nets:
  N1: U2.Q1, UDN_2981_-_8-Channel_Source_Driver2.In_2
  N2: U2.Q2, UDN_2981_-_8-Channel_Source_Driver2.In_3
  N3: U2.Q3, UDN_2981_-_8-Channel_Source_Driver2.In_4
  N4: U2.Q4, UDN_2981_-_8-Channel_Source_Driver2.In_5
  N5: U2.Q5, UDN_2981_-_8-Channel_Source_Driver2.In_6
  N6: U2.Q6, UDN_2981_-_8-Channel_Source_Driver2.In_7
  N7: U2.Q7, UDN_2981_-_8-Channel_Source_Driver2.In_8
  N8: U2.Q0, UDN_2981_-_8-Channel_Source_Driver2.In_1
  N9: U3.Q1, R31.Pin_1
  N10: U3.Q2, R30.Pin_1
  N11: U3.Q3, R32.Pin_1
  N12: U3.Q4, R27.Pin_1
  N13: U3.Q5, R25.Pin_1
  N14: U3.Q6, R28.Pin_1
  N15: U3.Q7, R26.Pin_1
  N16: U3.Q7', U4.DS
  N17: U3.Q0, R29.Pin_1
  N18: U4.Q1, R15.Pin_1
  N19: U4.Q2, R14.Pin_1
  N20: U4.Q3, R16.Pin_1
  N21: U4.Q4, R11.Pin_1
  N22: U4.Q5, R9.Pin_1
  N23: U4.Q6, R12.Pin_1
  N24: U4.Q7, R10.Pin_1
  N25: U4.Q7', U5.DS
  N26: U4.Q0, R13.Pin_1
  N27: U5.Q1, R23.Pin_1
  N28: U5.Q2, R22.Pin_1
  N29: U5.Q3, R24.Pin_1
  N30: U5.Q4, R19.Pin_1
  N31: U5.Q5, R17.Pin_1
  N32: U5.Q6, R20.Pin_1
  N33: U5.Q7, R18.Pin_1
  N34: U5.Q0, R21.Pin_1

notes:
  DS핀 파이 GPIO 연결
  OE핀 파이 GPIO 연결
  Latch(STCP)핀 파이 GPIO 연결
  CLK(SHCP)핀 파이 GPIO 연결
  RGB LED 애노드 8개 핀에 연결
  RGB LED RED 캐소드 8개 핀에 연결
  RGB LED GREEN 캐소드 8개 핀에 연결
  RGB LED BLUE 캐소드 8개 핀에 연결
  330Ω 저항

custom parts:
  DIP - 18 pins: Recommended for high-side switching applications that benefit from separate logic and load grounds, these devices encompass load supply voltages to 50 V and output currents to -500 mA. These 8-channel source drivers are useful for interfacing between low-level logic and high-current loads. Typical loads include relays, solenoids, lamps, stepper and/or servo motors, print hammers, and LEDs.
