# Fritzing sketch tmc2100 (saved by Fritzing 0.9.3b)

parts:
  TMC2101 = Pololu A4988 [package=SO16]
  JACK1 = 2.1mm Barrel Jack with Terminal Block
  M1 = Stepper Motor - Bipolar
  Raspberry_Pi_1 = Raspberry Pi 3 [part_number=RPI-3-V1.2]
  C1 = Electrolytic Capacitor [capacitance=0.1mF package="0605 [SMD, electrolytic]"]

nets:
  N1: TMC2101.ENABLE, Raspberry_Pi_1.GPIO23
  N2: TMC2101.STEP, Raspberry_Pi_1.GPIO21
  N3: TMC2101.DIR, Raspberry_Pi_1.GPIO20
  N4: TMC2101.GND#8, Raspberry_Pi_1.GND
  VDD: TMC2101.VDD, Raspberry_Pi_1.3v3
  N5: TMC2101.1B, M1.C
  N6: TMC2101.1A, M1.D
  N7: TMC2101.2A, M1.B
  N8: TMC2101.2B, M1.A
  N9: TMC2101.GND#14, JACK1.NEG, C1.-
  N10: TMC2101.VMOT, JACK1.POS, C1.+

notes:
  EN (GPIO 23)
  STEP (GPIO 21)
  DIR (GPIO 20)
  100uF
  12V
